// Logisim project bianary2dec8bit.circ as structural Verilog: 1 circuit, main circuit main
module main (
);

  wire bcd_to_7_segment_decoder_7_p1, button_1_out, button_2_out, button_3_out, button_4_out, button_5_out,
       button_6_out, button_8_out, n7_segment_display_1_p1, n7_segment_display_1_p2, n7_segment_display_2_p2,
       n7_segment_display_3_p2, n7_segment_display_4_p2, n7_segment_display_5_p2, n7_segment_display_6_p2,
       n7_segment_display_7_p2, n7_segment_display_9_p1, n7_segment_display_9_p2, n7_segment_display_10_p2;
  wire [3:0] bit_extender_1_out, bit_extender_2_out, bit_extender_3_out, bit_extender_4_out,
       bit_extender_5_out, bit_extender_6_out, bit_extender_7_out, bit_extender_8_out;
  wire [7:0] t_ff_8_q;

  // _7_Segment_Display 7_segment_display_1: pin names not known; wires that end beside it: n7_segment_display_1_p1, n7_segment_display_1_p2
  // _7_Segment_Display 7_segment_display_2: pin names not known; wires that end beside it: n7_segment_display_1_p2, n7_segment_display_2_p2
  // BCD_to_7_Segment_decoder bcd_to_7_segment_decoder_1: pin names not known
  // BCD_to_7_Segment_decoder bcd_to_7_segment_decoder_2: pin names not known
  Button button_1 (.out(button_1_out));
  T_Flip_Flop t_ff_1 (.T(1'b1), .clk(button_1_out), .Q(t_ff_8_q[7]));  // open: Qn, reset, preset
  T_Flip_Flop t_ff_2 (.T(1'b1), .clk(button_5_out), .Q(t_ff_8_q[3]));  // open: Qn, reset, preset
  // _7_Segment_Display 7_segment_display_3: pin names not known; wires that end beside it: n7_segment_display_2_p2, n7_segment_display_3_p2
  // BCD_to_7_Segment_decoder bcd_to_7_segment_decoder_3: pin names not known
  Button button_2 (.out(button_2_out));
  Button button_3 (.out(button_3_out));
  T_Flip_Flop t_ff_3 (.T(1'b1), .clk(button_2_out), .Q(t_ff_8_q[6]));  // open: Qn, reset, preset
  T_Flip_Flop t_ff_4 (.T(1'b1), .clk(button_6_out), .Q(t_ff_8_q[2]));  // open: Qn, reset, preset
  assign bit_extender_1_out = {{3{1'b0}}, t_ff_8_q[7]};  // Bit_Extender bit_extender_1
  assign bit_extender_2_out = {{3{1'b0}}, t_ff_8_q[6]};  // Bit_Extender bit_extender_2
  assign bit_extender_3_out = {{3{1'b0}}, t_ff_8_q[5]};  // Bit_Extender bit_extender_3
  assign bit_extender_4_out = {{3{1'b0}}, t_ff_8_q[4]};  // Bit_Extender bit_extender_4
  assign bit_extender_5_out = {{3{1'b0}}, t_ff_8_q[3]};  // Bit_Extender bit_extender_5
  assign bit_extender_6_out = {{3{1'b0}}, t_ff_8_q[2]};  // Bit_Extender bit_extender_6
  assign bit_extender_7_out = {{3{1'b0}}, t_ff_8_q[1]};  // Bit_Extender bit_extender_7
  assign bit_extender_8_out = {{3{1'b0}}, t_ff_8_q[0]};  // Bit_Extender bit_extender_8
  // _7_Segment_Display 7_segment_display_4: pin names not known; wires that end beside it: n7_segment_display_3_p2, n7_segment_display_4_p2
  // _7_Segment_Display 7_segment_display_5: pin names not known; wires that end beside it: n7_segment_display_4_p2, n7_segment_display_5_p2
  // BCD_to_7_Segment_decoder bcd_to_7_segment_decoder_4: pin names not known
  // BCD_to_7_Segment_decoder bcd_to_7_segment_decoder_5: pin names not known
  Button button_4 (.out(button_4_out));
  T_Flip_Flop t_ff_5 (.T(1'b1), .clk(button_3_out), .Q(t_ff_8_q[5]));  // open: Qn, reset, preset
  T_Flip_Flop t_ff_6 (.T(1'b1), .clk(bcd_to_7_segment_decoder_7_p1), .Q(t_ff_8_q[1]));  // open: Qn, reset, preset
  // _7_Segment_Display 7_segment_display_6: pin names not known; wires that end beside it: n7_segment_display_5_p2, n7_segment_display_6_p2
  // BCD_to_7_Segment_decoder bcd_to_7_segment_decoder_6: pin names not known
  Button button_5 (.out(button_5_out));
  Button button_6 (.out(button_6_out));
  T_Flip_Flop t_ff_7 (.T(1'b1), .clk(button_4_out), .Q(t_ff_8_q[4]));  // open: Qn, reset, preset
  T_Flip_Flop t_ff_8 (.T(1'b1), .clk(button_8_out), .Q(t_ff_8_q[0]));  // open: Qn, reset, preset
  // _7_Segment_Display 7_segment_display_7: pin names not known; wires that end beside it: n7_segment_display_6_p2, n7_segment_display_7_p2
  _7_Segment_Display u_7_segment_display_8 ();  // open: g, f, a, b, e, d, c, dp
  // BCD_to_7_Segment_decoder bcd_to_7_segment_decoder_7: pin names not known; wires that end beside it: bcd_to_7_segment_decoder_7_p1
  // BCD_to_7_Segment_decoder bcd_to_7_segment_decoder_8: pin names not known
  Button button_7 (.out(bcd_to_7_segment_decoder_7_p1));
  Button button_8 (.out(button_8_out));
  // Binary_to_BCD_converter #(.binvalue(4)) binary_to_bcd_converter_1: pin names not known; wires that end beside it: bit_extender_1_out, n7_segment_display_1_p1
  // Binary_to_BCD_converter #(.binvalue(4)) binary_to_bcd_converter_2: pin names not known; wires that end beside it: bit_extender_2_out, n7_segment_display_1_p2
  // Binary_to_BCD_converter #(.binvalue(4)) binary_to_bcd_converter_3: pin names not known; wires that end beside it: bit_extender_3_out, n7_segment_display_2_p2
  // Binary_to_BCD_converter #(.binvalue(4)) binary_to_bcd_converter_4: pin names not known; wires that end beside it: bit_extender_4_out, n7_segment_display_3_p2
  // Binary_to_BCD_converter #(.binvalue(4)) binary_to_bcd_converter_5: pin names not known; wires that end beside it: bit_extender_5_out, n7_segment_display_4_p2
  // Binary_to_BCD_converter #(.binvalue(4)) binary_to_bcd_converter_6: pin names not known; wires that end beside it: bit_extender_6_out, n7_segment_display_5_p2
  // Binary_to_BCD_converter #(.binvalue(4)) binary_to_bcd_converter_7: pin names not known; wires that end beside it: bit_extender_7_out, n7_segment_display_6_p2
  // Binary_to_BCD_converter #(.binvalue(4)) binary_to_bcd_converter_8: pin names not known; wires that end beside it: bit_extender_8_out, n7_segment_display_7_p2
  // _7_Segment_Display 7_segment_display_9: pin names not known; wires that end beside it: n7_segment_display_9_p1, n7_segment_display_9_p2
  // _7_Segment_Display 7_segment_display_10: pin names not known; wires that end beside it: n7_segment_display_9_p2, n7_segment_display_10_p2
  // BCD_to_7_Segment_decoder bcd_to_7_segment_decoder_9: pin names not known
  // BCD_to_7_Segment_decoder bcd_to_7_segment_decoder_10: pin names not known
  // Binary_to_BCD_converter #(.binvalue(8)) binary_to_bcd_converter_9: pin names not known; wires that end beside it: t_ff_8_q, n7_segment_display_9_p1, n7_segment_display_9_p2
  _7_Segment_Display u_7_segment_display_11 ();  // open: g, f, a, b, e, d, c, dp
  // BCD_to_7_Segment_decoder bcd_to_7_segment_decoder_11: pin names not known; wires that end beside it: n7_segment_display_10_p2
endmodule
